// Logisim project Übung3.circ as structural Verilog: 2 circuits, main circuit main
module main (
  input  in_1,
  input  in_2,
  input  in_3,
  input  in_4,
  input  in_5,
  input  in_6,
  input  in_7
);

  wire \volladdierer_1_übertrag , \volladdierer_2_übertrag ;
  wire [3:0] volladdierer_1_summe;

  Volladdierer volladdierer_1 (
    .in_1(in_1), ._2y(in_2), .\_3ü (in_3), .Summe(volladdierer_1_summe[0]),
    .\Übertrag (\volladdierer_1_übertrag ));
  Volladdierer volladdierer_2 (
    .in_1(in_4), ._2y(in_5), .\_3ü (\volladdierer_1_übertrag ), .Summe(volladdierer_1_summe[1]),
    .\Übertrag (\volladdierer_2_übertrag ));
  Volladdierer volladdierer_3 (
    .in_1(in_6), ._2y(in_7), .\_3ü (\volladdierer_2_übertrag ), .Summe(volladdierer_1_summe[2]),
    .\Übertrag (volladdierer_1_summe[3]));
  Hex_Digit_Display hex_digit_display_1 (.value(volladdierer_1_summe));  // open: dp
endmodule

module Volladdierer (
  input  in_1,
  input  _2y,
  input  \_3ü ,
  output Summe,
  output \Übertrag 
);

  wire and_1_out, and_2_out, xor_1_out;

  xor xor_1 (xor_1_out, in_1, _2y);
  and and_1 (and_1_out, in_1, _2y);
  xor xor_2 (Summe, xor_1_out, \_3ü );
  and and_2 (and_2_out, xor_1_out, \_3ü );
  or or_1 (\Übertrag , and_1_out, and_2_out);
endmodule
